# Fritzing sketch 16keys (saved by Fritzing 0.9.3b)
circuit board: 13.8834cm x 14.7424cm

parts:
  S1 = SWITCH-MOMENTARY-2 [package=tactile-pth-12mm]
  S2 = SWITCH-MOMENTARY-2 [package=tactile-pth-12mm]
  S3 = SWITCH-MOMENTARY-2 [package=tactile-pth-12mm]
  S4 = SWITCH-MOMENTARY-2 [package=tactile-pth-12mm]
  S5 = SWITCH-MOMENTARY-2 [package=tactile-pth-12mm]
  S7 = SWITCH-MOMENTARY-2 [package=tactile-pth-12mm]
  R1 = Resistor [tolerance=±5% resistance=1k package=THT]
  S6 = SWITCH-MOMENTARY-2 [package=tactile-pth-12mm]
  R4 = Resistor [tolerance=±5% resistance=220 package=THT]
  R5 = Resistor [tolerance=±5% resistance=220 package=THT]
  R2 = Resistor [tolerance=±5% resistance=1k package=THT]
  R6 = Resistor [tolerance=±5% resistance=220 package=THT]
  S9 = SWITCH-MOMENTARY-2 [package=tactile-pth-12mm]
  S10 = SWITCH-MOMENTARY-2 [package=tactile-pth-12mm]
  S11 = SWITCH-MOMENTARY-2 [package=tactile-pth-12mm]
  S12 = SWITCH-MOMENTARY-2 [package=tactile-pth-12mm]
  S13 = SWITCH-MOMENTARY-2 [package=tactile-pth-12mm]
  S14 = SWITCH-MOMENTARY-2 [package=tactile-pth-12mm]
  S15 = SWITCH-MOMENTARY-2 [package=tactile-pth-12mm]
  S16 = SWITCH-MOMENTARY-2 [package=tactile-pth-12mm]
  R7 = Resistor [tolerance=±5% resistance=1k package=THT]
  R8 = Resistor [tolerance=±5% resistance=1k package=THT]
  WeMos_D1_Mini1 = WeMos D1 Mini
  R9 = Resistor [tolerance=±5% resistance=10k package=THT]
  S8 = SWITCH-MOMENTARY-2 [package=tactile-pth-12mm]

nets:
  N1: S1.1, S2.1, S3.1, S4.1, R1.Pin_1, R2.Pin_0
  N2: S1.2, S5.2, R4.Pin_1, S9.2, S13.2, WeMos_D1_Mini1.A0, R9.Pin_1
  N3: S2.2, S6.2, R4.Pin_0, R5.Pin_1, S10.2, S14.2
  N4: S3.2, S7.2, R5.Pin_0, R6.Pin_1, S11.2, S15.2
  N5: S4.2, R6.Pin_0, S12.2, S16.2, S8.2
  N6: S5.1, S7.1, S6.1, R2.Pin_1, R7.Pin_0, S8.1
  N7: R1.Pin_0, WeMos_D1_Mini1.3V3
  N8: S9.1, S10.1, S11.1, S12.1, R7.Pin_1, R8.Pin_0
  N9: S13.1, S14.1, S15.1, S16.1, R8.Pin_1
  N10: WeMos_D1_Mini1.G, R9.Pin_0
