# Fritzing sketch Verdrahtungsplan (saved by Fritzing 0.9.3b)

parts:
  WeMos_D1_Mini1 = WeMos D1 Mini
  Bauteil1 = ws2812b [package="smd 2812b"]
  S1 = Momentary Switch [package=ksa_sealed_tac_switch]
  Bauteil2 = HC-SR501 Body Sensor Module
  Bauteil3 = ws2812b [package="smd 2812b"]
  Bauteil4 = ws2812b [package="smd 2812b"]

nets:
  5V: WeMos_D1_Mini1.5V, Bauteil1.VDD, Bauteil2.VCC
  N1: WeMos_D1_Mini1.D1, S1.3
  N2: WeMos_D1_Mini1.D5, Bauteil2.OUT
  N3: WeMos_D1_Mini1.D7, Bauteil1.DIN
  VSS: WeMos_D1_Mini1.G, Bauteil1.VSS, S1.4, Bauteil2.GND, Bauteil3.VSS, Bauteil4.VSS
  N4: Bauteil1.DOUT, Bauteil3.DIN
  N5: Bauteil3.DOUT, Bauteil4.DIN

custom parts:
  HC-SR501 Body Sensor Module: Pyroelectric Infrared PIR Motion Sensor Detector Module
